# Fritzing sketch reed_contact (saved by Fritzing 0.9.3b)
breadboards: 1

parts:
  WeMos_D1_Mini1 = WeMos D1 Mini
  S1 = Reed switch [package=THT]
  R1 = Resistor [tolerance=±5% resistance=1k package="1206 [SMD]"]  # not connected

nets:
  N1: WeMos_D1_Mini1.D1, S1.pin_2
  N2: WeMos_D1_Mini1.G, S1.pin_1
